# Fritzing sketch 01_10_2019_LCD_I2C_backlight_regulation (saved by Fritzing 0.9.3b)
circuit board: 8.46667cm x 5.64444cm
breadboards: 1

parts:
  Part1 = LCD screen
  part = LCM1602 IIC [chip_label="LCM1602 IIC" package="DIP (Dual Inline) [THT]"]
  Part2 = Arduino Uno (Rev3)

nets:
  VSS: Part1.VSS, part.VSS
  VDD: Part1.VDD, part.VDD
  N1: Part1.V0, part.V0
  N2: Part1.RS, part.RS
  N3: Part1.R/W, part.RW
  N4: Part1.E, part.E
  N5: Part1.DB0, part.D0
  N6: Part1.DB1, part.D1
  N7: Part1.DB2, part.D2
  N8: Part1.DB3, part.D3
  N9: Part1.DB4, part.D4
  N10: Part1.DB5, part.D5
  N11: Part1.DB6, part.D6
  N12: Part1.DB7, part.D7
  N13: Part1.LED+, part.A
  N14: Part1.LED-, part.K, Part2.D6_PWM
  GND: part.GND, Part2.GND
  VCC: part.VCC, Part2.5V
  N15: part.SDA, Part2.A4/SDA
  N16: part.SCL, Part2.A5/SCL

custom parts:
  LCM1602 IIC: I2C-Module to use a 1602 or 2004 LCD on with the wire.h libory Serial LCD Modul
